# Fritzing sketch fritzing (saved by Fritzing 0.9.5d)

parts:
  M1 = 1-chan-5v-relay-module_1
  U1 = ESP32-38PinWide [part_number=ESP32-38PinWide]
  M2 = 1-chan-5v-relay-module_1
  M3 = 1-chan-5v-relay-module_1
  M4 = 1-chan-5v-relay-module_1
  J1 = Piezo Speaker
  J2 = 220v plug
  LED5 = LEDs [package=led10mm]
  LED4 = LEDs [package=led10mm]
  LED7 = LEDs [package=led10mm]
  LED6 = LEDs [package=led10mm]

nets:
  N1: M1.connector1, U1.GND, M2.connector1, M3.connector1, M4.connector1, J1.pin1
  N2: M1.connector2, U1.GPIO26
  N3: M1.connector3, LED4.A
  N4: M1.connector4, M2.connector4, M3.connector4, M4.connector4, J2.pin2
  N5: U1.GPIO32, M4.connector2
  N6: U1.GPIO33, M3.connector2
  N7: U1.GPIO25, M2.connector2
  N8: U1.GPIO5, J1.pin2
  N9: M2.connector3, LED5.A
  N10: M3.connector3, LED7.A
  N11: M4.connector3, LED6.A
  N12: J2.pin1, LED5.C, LED7.C, LED6.C

custom parts:
  ESP32-38PinWide: Generic 38-Pin ESP32 with wide format (only access to one side of pins on a breadboard) based on Stephen Lilley's HiLetgo ESP-WROOM-32 ESP32 ESP-32S Development Board.
  220v plug: Generic 220V AC plug.
  LEDs: LEDs Standard schematic elements and footprints for 5mm, 3mm, 1206, and 0603 sized LEDs. 5mm - Spark Fun Electronics SKU : COM-00529 (and others)
